# Fritzing sketch 01_Led_Resistor (saved by Fritzing 0.9.4)
breadboards: 1

parts:
  WeMos_D1_Mini6 = WeMos D1 Mini  # not connected
  WeMos_D1_Mini7 = WeMos D1 Mini  # not connected
  WeMos_D1_Mini8 = WeMos D1 Mini  # not connected
  WeMos_D1_Mini9 = WeMos D1 Mini  # not connected
  WeMos_D1_Mini10 = WeMos D1 Mini  # not connected
  LED6 = LED - 5mm [color="Red (633nm)" package="5 mm [THT]"]
  R6 = Resistor [tolerance=±5% resistance=220 package=THT]
  USBTTL2 = USB TTL Serial Cable  # not connected

nets:
  N1: LED6.cathode, R6.Pin_1

notes:
  WeMos D1 mini
  Female above
  Male above
  Male below
  no headers
  No headers
  Header configurations
  Varios Cables Dupont Macho-Macho
  MATERIALES
  Open Source 2021
  Andrés Weitzel
  1 Cable MicroUSB de Datos
  1 Diodo Led
  1 Resistor (220 ohms)
  1 ESP8266(Wemos D1 Mini)
  Diodo y Resistor

custom parts:
  WeMos D1 Mini: The D1 mini is a mini wifi board based on ESP-8266EX.
  WeMos D1 Mini: The D1 mini is a mini wifi board based on ESP-8266EX.
