# Fritzing sketch 02_Secuencia_Varios_Leds (saved by Fritzing 0.9.4)
breadboards: 1

parts:
  WeMos_D1_Mini4 = WeMos D1 Mini  # not connected
  WeMos_D1_Mini3 = WeMos D1 Mini  # not connected
  WeMos_D1_Mini1 = WeMos D1 Mini  # not connected
  WeMos_D1_Mini2 = WeMos D1 Mini  # not connected
  WeMos_D1_Mini5 = WeMos D1 Mini  # not connected
  LED1 = LED - 5mm [color="Red (633nm)" package="5 mm [THT]"]
  R1 = Resistor [tolerance=±5% resistance=220 package=THT]
  LED2 = LED - 5mm [color="Red (633nm)" package="5 mm [THT]"]
  R2 = Resistor [tolerance=±5% resistance=220 package=THT]
  LED3 = LED - 5mm [color="Red (633nm)" package="5 mm [THT]"]
  R3 = Resistor [tolerance=±5% resistance=220 package=THT]
  LED4 = LED - 5mm [color="Red (633nm)" package="5 mm [THT]"]
  R4 = Resistor [tolerance=±5% resistance=220 package=THT]
  LED5 = LED - 5mm [color="Red (633nm)" package="5 mm [THT]"]
  R5 = Resistor [tolerance=±5% resistance=220 package=THT]
  USBTTL1 = USB TTL Serial Cable  # not connected

nets:
  N1: LED1.cathode, R1.Pin_1
  N2: R1.Pin_0, R2.Pin_0, R3.Pin_0, R4.Pin_0, R5.Pin_0
  N3: LED2.cathode, R2.Pin_1
  N4: LED3.cathode, R3.Pin_1
  N5: LED4.cathode, R5.Pin_1
  N6: R4.Pin_1, LED5.cathode

notes:
  Female above
  Male above
  Male below
  No headers
  no headers
  Header configurations
  WeMos D1 mini
  1 ESP8266(Wemos D1 Mini)
  5 Resistores (220 ohms)
  5 Diodos Leds
  1 Cable MicroUSB de Datos
  Andrés Weitzel
  Open Source 2021
  MATERIALES
  Varios Cables Dupont Macho-Macho
  Secuencia_Leds

custom parts:
  WeMos D1 Mini: The D1 mini is a mini wifi board based on ESP-8266EX.
  WeMos D1 Mini: The D1 mini is a mini wifi board based on ESP-8266EX.
