# Fritzing sketch 03_Led_Boton_Pulsador (saved by Fritzing 0.9.4)
breadboards: 1

parts:
  WeMos_D1_Mini6 = WeMos D1 Mini  # not connected
  WeMos_D1_Mini7 = WeMos D1 Mini  # not connected
  WeMos_D1_Mini8 = WeMos D1 Mini  # not connected
  WeMos_D1_Mini9 = WeMos D1 Mini  # not connected
  WeMos_D1_Mini10 = WeMos D1 Mini  # not connected
  LED6 = LED - 5mm [color="Red (633nm)" package="5 mm [THT]"]
  R6 = Resistor [tolerance=±5% resistance=220 package=THT]
  R10 = Resistor [tolerance=±5% resistance=4.7k package=THT]
  USBTTL2 = USB TTL Serial Cable  # not connected
  S4 = Momentary Switch [package=ksa_sealed_tac_switch]

nets:
  N1: LED6.cathode, R6.Pin_1
  N2: R6.Pin_0, R10.Pin_0
  N3: R10.Pin_1, S4.1, S4.2
  N4: S4.3, S4.4

notes:
  WeMos D1 mini
  Female above
  Male above
  Male below
  no headers
  No headers
  Header configurations
  Varios Cables Dupont Macho-Macho
  MATERIALES
  Led_Boton_Pulsador
  Open Source 2021
  Andrés Weitzel
  1 Cable MicroUSB de Datos
  1 Diodo Led
  1  Resistor (220 ohms)
  1 ESP8266(Wemos D1 Mini)
  1  Resistor (4.7k)
  1  Boton Pulsador

custom parts:
  WeMos D1 Mini: The D1 mini is a mini wifi board based on ESP-8266EX.
  WeMos D1 Mini: The D1 mini is a mini wifi board based on ESP-8266EX.
