# Fritzing sketch 04_Led_Boton_Pulsador_Con_Testigo (saved by Fritzing 0.9.4)
breadboards: 1

parts:
  WeMos_D1_Mini11 = WeMos D1 Mini  # not connected
  WeMos_D1_Mini12 = WeMos D1 Mini  # not connected
  WeMos_D1_Mini13 = WeMos D1 Mini  # not connected
  WeMos_D1_Mini14 = WeMos D1 Mini  # not connected
  WeMos_D1_Mini15 = WeMos D1 Mini  # not connected
  LED7 = LED - 5mm [color="Red (633nm)" package="5 mm [THT]"]
  R11 = Resistor [tolerance=±5% resistance=220 package=THT]
  R12 = Resistor [tolerance=±5% resistance=4.7k package=THT]
  USBTTL3 = USB TTL Serial Cable  # not connected
  LED8 = LED - 5mm [color="Red (633nm)" package="5 mm [THT]"]
  R13 = Resistor [tolerance=±5% resistance=220 package=THT]
  S3 = Momentary Switch [package=ksa_sealed_tac_switch]

nets:
  N1: LED7.cathode, R11.Pin_1
  N2: R11.Pin_0, R12.Pin_0, R13.Pin_0
  N3: R12.Pin_1, S3.3, S3.4
  N4: LED8.cathode, R13.Pin_1
  N5: S3.1, S3.2

notes:
  WeMos D1 mini
  Female above
  Male above
  Male below
  no headers
  No headers
  Header configurations
  Varios Cables Dupont Macho-Macho
  MATERIALES
  Led_Boton_Pulsador_Con_Testigo
  Open Source 2021
  Andrés Weitzel
  1 Cable MicroUSB de Datos
  2 Diodos Leds
  1  Boton Pulsador
  1  Resistor (4.7k)
  2  Resistores (220 ohms)
  1 ESP8266(Wemos D1 Mini)
  Led Testigo

custom parts:
  WeMos D1 Mini: The D1 mini is a mini wifi board based on ESP-8266EX.
  WeMos D1 Mini: The D1 mini is a mini wifi board based on ESP-8266EX.
