# Fritzing sketch 05_Leds_Botones_Pulsadores_Con_Testigo (saved by Fritzing 0.9.4)
breadboards: 1

parts:
  WeMos_D1_Mini16 = WeMos D1 Mini  # not connected
  WeMos_D1_Mini17 = WeMos D1 Mini  # not connected
  WeMos_D1_Mini18 = WeMos D1 Mini  # not connected
  WeMos_D1_Mini19 = WeMos D1 Mini  # not connected
  WeMos_D1_Mini20 = WeMos D1 Mini  # not connected
  LED9 = LED - 5mm [color="Red (633nm)" package="5 mm [THT]"]
  LED10 = LED - 5mm [color="Red (633nm)" package="5 mm [THT]"]
  R14 = Resistor [tolerance=±5% resistance=220 package=THT]
  R15 = Resistor [tolerance=±5% resistance=220 package=THT]
  R16 = Resistor [tolerance=±5% resistance=4.7k package=THT]
  USBTTL4 = USB TTL Serial Cable  # not connected
  S4 = Momentary Switch [package=ksa_sealed_tac_switch]
  R17 = Resistor [tolerance=±5% resistance=4.7k package=THT]
  S5 = Momentary Switch [package=ksa_sealed_tac_switch]
  LED11 = LED - 5mm [color="Red (633nm)" package="5 mm [THT]"]
  R18 = Resistor [tolerance=±5% resistance=220 package=THT]

nets:
  N1: LED9.cathode, R15.Pin_1
  N2: LED10.cathode, R14.Pin_1
  N3: R14.Pin_0, R15.Pin_0, R16.Pin_0, R17.Pin_0, R18.Pin_0
  N4: R16.Pin_1, S4.1, S4.2
  N5: S4.3, S4.4, S5.3, S5.4
  N6: R17.Pin_1, S5.1, S5.2
  N7: LED11.cathode, R18.Pin_1

notes:
  WeMos D1 mini
  Female above
  Male above
  Male below
  no headers
  No headers
  Header configurations
  Varios Cables Dupont Macho-Macho
  MATERIALES
  Leds_Botones_Pulsadores_Con_Testigo
  Open Source 2021
  Andrés Weitzel
  1 Cable MicroUSB de Datos
  3 Diodos Leds
  Led Testigo
  2  Botones Pulsadores
  2  Resistores (4.7k)
  3  Resistores (220 ohms)
  1 ESP8266(Wemos D1 Mini)

custom parts:
  WeMos D1 Mini: The D1 mini is a mini wifi board based on ESP-8266EX.
  WeMos D1 Mini: The D1 mini is a mini wifi board based on ESP-8266EX.
